// Digital circuit lab2_part2.dig as structural Verilog
module lab2_part2 (
  input  in0,
  input  in1,
  input  in2,
  input  in3,
  output seg_a,
  output seg_f,
  output seg_b,
  output seg_g,
  output seg_e,
  output seg_c,
  output seg_d,
  output seg_dp,
  output sign_a,
  output sign_f,
  output sign_b,
  output sign_g,
  output sign_e,
  output sign_c,
  output sign_d,
  output sign_dp,
  output carry
);

  wire and_1_out, and_2_out, and_3_out, and_4_out, and_5_out, and_6_out, and_7_out, and_8_out,
       multiplexer_7_out, not_1_out, not_2_out, not_3_out, not_4_out, not_5_out, not_6_out, not_7_out,
       not_8_out, not_9_out, not_10_out, not_11_out, not_12_out, not_13_out, not_14_out, not_15_out,
       not_16_out, not_17_out, not_18_out, not_19_out, not_20_out, not_21_out, not_22_out, not_23_out,
       not_24_out, not_25_out, not_26_out, or_1_out, xor_1_out, xor_3_out;
  wire [2:0] multiplexer_1_out, xor_2_out;

  not not_1 (not_1_out, in1);
  not not_2 (not_2_out, in0);
  xor xor_1 (xor_1_out, not_1_out, 1'b0);
  and and_1 (and_1_out, not_1_out, 1'b0);
  and and_2 (and_2_out, not_2_out, 1'b1);
  xor xor_2 (xor_2_out[0], not_2_out, 1'b1);
  not not_3 (not_3_out, in2);
  xor xor_3 (xor_3_out, not_3_out, 1'b0);
  and and_3 (and_3_out, not_3_out, 1'b0);
  xor xor_4 (xor_2_out[1], xor_1_out, and_2_out);
  and and_4 (and_4_out, xor_1_out, and_2_out);
  or or_1 (or_1_out, and_1_out, and_4_out);
  xor xor_5 (xor_2_out[2], xor_3_out, or_1_out);
  and and_5 (and_5_out, xor_3_out, or_1_out);
  or or_2 (carry, and_3_out, and_5_out);
  Multiplexer #(.Bits(3)) multiplexer_1 (.sel(in3), .in_0({in2, in1, in0}), .in_1(xor_2_out), .out(multiplexer_1_out));
  Seven_Seg seven_seg_1 (.a(1'b0), .b(1'b0), .c(1'b0), .d(1'b0), .e(1'b0), .f(1'b0), .g(in3), .dp(1'b0));
  not not_4 (not_4_out, 1'b1);
  not not_5 (not_5_out, 1'b1);
  not not_6 (not_6_out, 1'b1);
  not not_7 (not_7_out, 1'b1);
  not not_8 (not_8_out, 1'b1);
  not not_9 (not_9_out, 1'b1);
  not not_10 (not_10_out, 1'b1);
  Multiplexer #(.Selector_Bits(3)) multiplexer_2 (
    .sel(multiplexer_1_out), .in_0(1'b1), .in_1(not_4_out), .in_2(1'b1), .in_3(1'b1), .in_4(not_5_out),
    .in_5(1'b1), .in_6(1'b1), .in_7(1'b1), .out(seg_a));
  Multiplexer #(.Selector_Bits(3)) multiplexer_3 (
    .sel(multiplexer_1_out), .in_0(1'b1), .in_1(not_6_out), .in_2(1'b1), .in_3(not_7_out), .in_4(not_8_out),
    .in_5(not_9_out), .in_6(1'b1), .in_7(not_10_out), .out(seg_e));
  Seven_Seg seven_seg_2 (.a(seg_a), .b(seg_b), .c(seg_c), .d(seg_d), .e(seg_e), .f(seg_f), .g(seg_g), .dp(1'b0));
  Multiplexer #(.Selector_Bits(3)) multiplexer_4 (
    .sel(multiplexer_1_out), .in_0(1'b1), .in_1(1'b1), .in_2(1'b1), .in_3(1'b1), .in_4(1'b1),
    .in_5(not_11_out), .in_6(not_12_out), .in_7(1'b1), .out(seg_b));
  not not_11 (not_11_out, 1'b1);
  not not_12 (not_12_out, 1'b1);
  Multiplexer #(.Selector_Bits(3)) multiplexer_5 (
    .sel(multiplexer_1_out), .in_0(1'b1), .in_1(not_13_out), .in_2(not_14_out), .in_3(not_15_out),
    .in_4(1'b1), .in_5(1'b1), .in_6(1'b1), .in_7(not_16_out), .out(seg_f));
  not not_13 (not_13_out, 1'b1);
  not not_14 (not_14_out, 1'b1);
  not not_15 (not_15_out, 1'b1);
  not not_16 (not_16_out, 1'b1);
  Multiplexer #(.Selector_Bits(3)) multiplexer_6 (
    .sel(multiplexer_1_out), .in_0(1'b1), .in_1(1'b1), .in_2(not_17_out), .in_3(1'b1), .in_4(1'b1),
    .in_5(1'b1), .in_6(1'b1), .in_7(1'b1), .out(seg_c));
  not not_17 (not_17_out, 1'b1);
  Multiplexer #(.Selector_Bits(3)) multiplexer_7 (
    .sel(multiplexer_1_out), .in_0(not_18_out), .in_1(not_19_out), .in_2(1'b1), .in_3(1'b1), .in_4(1'b1),
    .in_5(1'b1), .in_6(1'b1), .in_7(not_20_out), .out(multiplexer_7_out));
  not not_18 (not_18_out, 1'b1);
  not not_19 (not_19_out, 1'b1);
  not not_20 (not_20_out, 1'b1);
  not not_21 (not_21_out, in0);
  not not_22 (not_22_out, in1);
  not not_23 (not_23_out, in2);
  not not_24 (not_24_out, 1'b1);
  not not_25 (not_25_out, 1'b1);
  not not_26 (not_26_out, 1'b1);
  and and_6 (and_6_out, not_21_out, not_22_out);
  Multiplexer #(.Selector_Bits(3)) multiplexer_8 (
    .sel(multiplexer_1_out), .in_0(1'b1), .in_1(not_24_out), .in_2(1'b1), .in_3(1'b1), .in_4(not_25_out),
    .in_5(1'b1), .in_6(1'b1), .in_7(not_26_out), .out(seg_d));
  and and_7 (and_7_out, and_6_out, not_23_out);
  and and_8 (and_8_out, and_7_out, in3);
  xor xor_6 (seg_g, multiplexer_7_out, and_8_out);

  assign seg_dp = 1'b0;
  assign sign_a = 1'b0;
  assign sign_b = 1'b0;
  assign sign_c = 1'b0;
  assign sign_d = 1'b0;
  assign sign_dp = 1'b0;
  assign sign_e = 1'b0;
  assign sign_f = 1'b0;
  assign sign_g = in3;

  // Notes on the sheet:
  //   Interface (do not edit the content inside this box)
  //   Outputs:
  //   Inputs
  //   Sign
  //   Decimal Number
endmodule

/* Test case:
in3 in2 in1 in0  sign_a sign_b sign_c sign_d sign_e sign_f sign_g  seg_a seg_b seg_c seg_d seg_e seg_f seg_g
 0   0   0   0    0      0      0      0      0      0      0       1     1     1     1     1     1     0
*/
