// Digital circuit lab2_part3.dig as structural Verilog
module lab2_part3 (
  input  clk,
  input  in0,
  input  in1,
  input  in2,
  input  in3,
  input  sel_write_1,
  input  sel_write_0,
  input  sel_readA_1,
  input  sel_readA_0,
  input  sel_readB_1,
  input  sel_readB_0,
  output out0,
  output out1,
  output out2,
  output out3,
  output reg0_0,
  output reg0_1,
  output reg0_2,
  output reg0_3,
  output reg1_0,
  output reg1_1,
  output reg1_2,
  output reg1_3,
  output reg2_0,
  output reg2_1,
  output reg2_2,
  output reg2_3,
  output reg3_0,
  output reg3_1,
  output reg3_2,
  output reg3_3,
  output inA_0,
  output inA_1,
  output inA_2,
  output inA_3,
  output inB_0,
  output inB_1,
  output inB_2,
  output inB_3
);

  wire multiplexer_1_out, multiplexer_2_out, multiplexer_3_out, multiplexer_5_out, not_1_out, not_2_out,
       not_3_out, not_4_out, not_5_out, not_6_out, not_7_out, not_8_out, not_9_out, not_10_out, not_11_out,
       not_12_out;

  Multiplexer #(.Selector_Bits(2)) multiplexer_1 (
    .sel({sel_write_1, sel_write_0}), .in_0(not_1_out), .in_1(not_2_out), .in_2(not_3_out), .in_3(1'b1),
    .out(multiplexer_1_out));
  not not_1 (not_1_out, 1'b1);
  not not_2 (not_2_out, 1'b1);
  not not_3 (not_3_out, 1'b1);
  Register #(.Bits(4)) Register_3 (
    .D({in3, in2, in1, in0}), .C(clk), .en(multiplexer_1_out), .Q({reg3_3, reg3_2, reg3_1, reg3_0}));
  Multiplexer #(.Selector_Bits(2)) multiplexer_2 (
    .sel({sel_write_1, sel_write_0}), .in_0(not_4_out), .in_1(not_5_out), .in_2(1'b1), .in_3(not_6_out),
    .out(multiplexer_2_out));
  not not_4 (not_4_out, 1'b1);
  not not_5 (not_5_out, 1'b1);
  not not_6 (not_6_out, 1'b1);
  Register #(.Bits(4)) Register_2 (
    .D({in3, in2, in1, in0}), .C(clk), .en(multiplexer_2_out), .Q({reg2_3, reg2_2, reg2_1, reg2_0}));
  Multiplexer #(.Selector_Bits(2)) multiplexer_3 (
    .sel({sel_write_1, sel_write_0}), .in_0(not_7_out), .in_1(1'b1), .in_2(not_8_out), .in_3(not_9_out),
    .out(multiplexer_3_out));
  not not_7 (not_7_out, 1'b1);
  not not_8 (not_8_out, 1'b1);
  not not_9 (not_9_out, 1'b1);
  Register #(.Bits(4)) Register_1 (
    .D({in3, in2, in1, in0}), .C(clk), .en(multiplexer_3_out), .Q({reg1_3, reg1_2, reg1_1, reg1_0}));
  Multiplexer #(.Selector_Bits(2)) multiplexer_4 (
    .sel({inB_1, inB_0}), .in_0(inA_3), .in_1(inA_0), .in_2(inA_1), .in_3(inA_2), .out(out1));
  Multiplexer #(.Selector_Bits(2)) multiplexer_5 (
    .sel({sel_write_1, sel_write_0}), .in_0(1'b1), .in_1(not_10_out), .in_2(not_11_out), .in_3(not_12_out),
    .out(multiplexer_5_out));
  not not_10 (not_10_out, 1'b1);
  not not_11 (not_11_out, 1'b1);
  not not_12 (not_12_out, 1'b1);
  Multiplexer #(.Selector_Bits(2)) multiplexer_6 (
    .sel({inB_1, inB_0}), .in_0(inA_2), .in_1(inA_3), .in_2(inA_0), .in_3(inA_1), .out(out2));
  Multiplexer #(.Bits(4), .Selector_Bits(2)) multiplexer_7 (
    .sel({sel_readA_1, sel_readA_0}), .in_0({reg0_3, reg0_2, reg0_1, reg0_0}),
    .in_1({reg1_3, reg1_2, reg1_1, reg1_0}), .in_2({reg2_3, reg2_2, reg2_1, reg2_0}),
    .in_3({reg3_3, reg3_2, reg3_1, reg3_0}), .out({inA_3, inA_2, inA_1, inA_0}));
  Multiplexer #(.Selector_Bits(2), .Bits(4)) multiplexer_8 (
    .sel({sel_readB_1, sel_readB_0}), .in_0({reg0_3, reg0_2, reg0_1, reg0_0}),
    .in_1({reg1_3, reg1_2, reg1_1, reg1_0}), .in_2({reg2_3, reg2_2, reg2_1, reg2_0}),
    .in_3({reg3_3, reg3_2, reg3_1, reg3_0}), .out({inB_3, inB_2, inB_1, inB_0}));
  Register #(.Bits(4)) Register_0 (
    .D({in3, in2, in1, in0}), .C(clk), .en(multiplexer_5_out), .Q({reg0_3, reg0_2, reg0_1, reg0_0}));
  Multiplexer #(.Selector_Bits(2)) multiplexer_9 (
    .sel({inB_1, inB_0}), .in_0(inA_1), .in_1(inA_2), .in_2(inA_3), .in_3(inA_0), .out(out3));
  Multiplexer #(.Selector_Bits(2)) multiplexer_10 (
    .sel({inB_1, inB_0}), .in_0(inA_0), .in_1(inA_1), .in_2(inA_2), .in_3(inA_3), .out(out0));
  Seven_Seg_Hex seven_seg_hex_1 (.d({inA_3, inA_2, inA_1, inA_0}), .dp(1'b0));
  Seven_Seg_Hex seven_seg_hex_2 (.d({reg3_3, reg3_2, reg3_1, reg3_0}), .dp(1'b0));
  Seven_Seg_Hex seven_seg_hex_3 (.d({in3, in2, in1, in0}), .dp(1'b0));
  Seven_Seg_Hex seven_seg_hex_4 (.d({inB_3, inB_2, inB_1, inB_0}), .dp(1'b0));
  Seven_Seg_Hex seven_seg_hex_5 (.d({reg2_3, reg2_2, reg2_1, reg2_0}), .dp(1'b0));
  Seven_Seg_Hex seven_seg_hex_6 (.d({2'b00, sel_write_1, sel_write_0}), .dp(1'b0));
  Seven_Seg_Hex seven_seg_hex_7 (.d({2'b00, sel_readA_1, sel_readA_0}), .dp(1'b0));
  Seven_Seg_Hex seven_seg_hex_8 (.d({out3, out2, out1, out0}), .dp(1'b0));
  Seven_Seg_Hex seven_seg_hex_9 (.d({reg1_3, reg1_2, reg1_1, reg1_0}), .dp(1'b0));
  Seven_Seg_Hex seven_seg_hex_10 (.d({2'b00, sel_readB_1, sel_readB_0}), .dp(1'b0));
  Seven_Seg_Hex seven_seg_hex_11 (.d({reg0_3, reg0_2, reg0_1, reg0_0}), .dp(1'b0));

  // Notes on the sheet:
  //   Interface (do not edit the content inside this box)
  //   Inputs
  //   Keypad
  //   Outputs
  //   Registers
  //   Values read into ALU inputs
  //   Rotatee
  //   Register 3
  //   Synchronizing Clock
  //   Rotation amount:
  //   Register Selection: Write-to
  //   Register 2
  //   Register Selection: Read-from
  //   ALU Output
  //   ALU input A register address:
  //   Register 1
  //   ALU input B register address:
  //   Register 0
endmodule

/* Test case:
clk in3 in2 in1 in0 sel^write_1 sel^write_0 sel^readA_1 sel^readA_0 sel^readB_1 sel^readB_0  reg3_3 reg3_2 reg3_1 reg3_0 reg2_3 reg2_2 reg2_1 reg2_0 reg1_3 reg1_2 reg1_1 reg1_0 reg0_3 reg0_2 reg0_1 reg0_0 out3 out2 out1 out0
 0   0   0   0   0   0           0           0           0           0           0            0      0      0      0      0      0      0      0      0      0      0      0      0      0      0      0      0    0    0    0
 1   0   0   0   0   0           0           0           0           0           0            0      0      0      0      0      0      0      0      0      0      0      0      0      0      0      0      0    0    0    0
 0   0   1   0   1   1           1           0           0           0           0            0      0      0      0      0      0      0      0      0      0      0      0      0      0      0      0      0    0    0    0
 1   0   1   0   1   1           1           0           0           0           0            0      1      0      1      0      0      0      0      0      0      0      0      0      0      0      0      0    0    0    0
 0   0   0   0   1   0           1           0           0           0           0            0      1      0      1      0      0      0      0      0      0      0      0      0      0      0      0      0    0    0    0
 1   0   0   0   1   0           1           0           0           0           0            0      1      0      1      0      0      0      0      0      0      0      1      0      0      0      0      0    0    0    0
 0   0   0   0   0   0           0           1           1           0           1            0      1      0      1      0      0      0      0      0      0      0      1      0      0      0      0      1    0    1    0
 1   0   0   0   0   0           0           1           1           0           1            0      1      0      1      0      0      0      0      0      0      0      1      0      0      0      0      1    0    1    0
 0   0   0   0   0   0           0           0           1           1           1            0      1      0      1      0      0      0      0      0      0      0      1      0      0      0      0      0    0    1    0
 1   0   0   0   0   0           0           0           1           1           1            0      1      0      1      0      0      0      0      0      0      0      1      0      0      0      0      0    0    1    0
*/
